# Fritzing sketch BrewController (saved by Fritzing 0.9.3b)
circuit board: 12.2cm x 6.1cm
breadboards: 1

parts:
  R2 = Resistor [tolerance=±5% resistance=4.7k package=THT]
  BUZZER = Piezo Speaker - PC Mount [part_number=COM-07950]
  Q1_BC548 = TRANSISTOR_NPN [package=to-92-ammo]
  R7 = Resistor [tolerance=±5% resistance=1k package=THT]
  Q1_BC549 = TRANSISTOR_NPN [package=to-92-ammo]
  R8 = Resistor [tolerance=±5% resistance=1k package=THT]
  R10 = Resistor [tolerance=±5% resistance=1k package=THT]
  Q1_BC550 = TRANSISTOR_NPN [package=to-92-ammo]
  R9 = Resistor [tolerance=±5% resistance=1k package=THT]
  HEATER_LED = LED - 3mm [color="Red (633nm)" package="3 mm [THT]"]
  AGITATOR_LED = LED - 3mm [color="Red (633nm)" package="3 mm [THT]"]
  HEATER = screw terminal, 2 pins
  AGITATOR = screw terminal, 2 pins
  ESP8266 = NodeMCU V1.0
  TEMPERATUR = screw terminal, 3 pins
  DISPLAY = 2.4" TFT LCD screen, SPI, Touch-enabled

nets:
  N1: R2.Pin_0, ESP8266.SD3, TEMPERATUR.pin2
  N2: R2.Pin_1, HEATER.pin2, AGITATOR.pin2, ESP8266.Vin, TEMPERATUR.pin3
  N3: BUZZER.GND, Q1_BC548.E
  VCC: BUZZER.VCC, ESP8266.3V3, DISPLAY.VCC
  N4: Q1_BC548.B, R7.Pin_0
  GND: Q1_BC548.C, Q1_BC549.C, Q1_BC550.C, R9.Pin_0, ESP8266.GND, TEMPERATUR.pin1, DISPLAY.GND
  N5: R7.Pin_1, ESP8266.SD2
  N6: Q1_BC549.E, HEATER.pin1
  N7: Q1_BC549.B, R8.Pin_0
  N8: R8.Pin_1, HEATER_LED.anode, ESP8266.RX
  N9: R10.Pin_0, Q1_BC550.B
  N10: R10.Pin_1, AGITATOR_LED.anode, ESP8266.TX
  N11: Q1_BC550.E, AGITATOR.pin1
  N12: R9.Pin_1, HEATER_LED.cathode, AGITATOR_LED.cathode
  N13: ESP8266.D1, DISPLAY.CS
  N14: ESP8266.D2, DISPLAY.DC
  N15: ESP8266.D3, DISPLAY.T_CS
  N16: ESP8266.D4, DISPLAY.T_IRQ
  N17: ESP8266.D5, DISPLAY.T_CLK, DISPLAY.SCL
  N18: ESP8266.D6, DISPLAY.T_DO, DISPLAY.SDO
  N19: ESP8266.D7, DISPLAY.T_DIN, DISPLAY.SDA
  N20: ESP8266.D8, DISPLAY.LED
  N21: ESP8266.RST, DISPLAY.RESET

notes:
  Temp-Sensor: DS18B20
  Trans: BC548
  BrewController v1.2
  +
  -

custom parts:
  Piezo Speaker - PC Mount: This is a small 12mm round speaker that operates around the audible 2kHz range. You can use these speakers to create simple music or user interfaces. Each speaker is PTH solderable and requires an operating voltage of 3.5-5V with a mean current of 35mA max. These speakers also have a typical sound output of 95 dBA and a coil resistance of 42 ±6.3 ohms.
  NodeMCU V1.0: ESP8266 based NodeMCU
  2.4" TFT LCD screen, SPI, Touch-enabled: 2.4", ILI9341-based TFT LCD screen with touch-sensing using the XPT2046 controller, SPI-compatible. There is also an SD-card version that is non-touch enabled but uses exactly the same board and pinout. This part is for both, though it should be noted that the SD reader and the touch screen are mutually incompatible
